// Logisim project Kombinacione mreže.circ as structural Verilog: 1 circuit, main circuit main
module main (
  input  in_1,
  input  in_2,
  input  in_3,
  input  in_4
);

  wire A_out, and_1_out, and_2_out, and_3_out, and_4_out, and_5_out, B_out, C_out, D_out, or_1_out;

  not A (A_out, in_1);
  not B (B_out, in_2);
  not C (C_out, in_3);
  not D (D_out, in_4);
  and and_1 (and_1_out, A_out, B_out, C_out, in_4);
  and and_2 (and_2_out, A_out, B_out, in_3, D_out);
  and and_3 (and_3_out, A_out, in_2, C_out, in_4);
  and and_4 (and_4_out, A_out, in_2, in_3, D_out);
  and and_5 (and_5_out, in_1, B_out, C_out, in_4);
  or or_1 (or_1_out, and_1_out, and_2_out, and_3_out, and_4_out, and_5_out);
  LED led_1 (.in(or_1_out));
endmodule
