// Logisim project Optimizacija logičkih kola.circ as structural Verilog: 1 circuit, main circuit main
module main (
  input  A,
  input  B,
  input  C
);

  wire and_1_out, and_2_out, not_1_out, not_2_out, or_1_out;

  not not_1 (not_1_out, A);
  not not_2 (not_2_out, B);
  and and_1 (and_1_out, not_1_out, not_2_out);
  and and_2 (and_2_out, A, B, C);
  // Probe on and_1_out
  // Probe on and_2_out
  // Probe on or_1_out
  or or_1 (or_1_out, and_1_out, and_2_out);
endmodule
